// Logisim project cpu.circ as structural Verilog: 4 circuits, main circuit main
module main (
  input  [29:0] in_1
);

  wire and_1_out, clock_1_out, demultiplexer_2_out0, demultiplexer_2_out1, demultiplexer_2_out2;
  wire [7:0] A_q, alu_1_output, D_q, demultiplexer_1_out0, demultiplexer_1_out1, demultiplexer_1_out2,
       multiplexer_1_out, multiplexer_2_out, multiplexer_3_out, pc_1_out, ram_1_data;
  wire [29:0] rom_1_data;

  Multiplexer #(.width(8), .enable("false")) multiplexer_1 (
    .in0(demultiplexer_1_out0), .in1(rom_1_data[25:18]), .out(multiplexer_1_out), .sel(rom_1_data[17]));
  Clock clock_1 (.out(clock_1_out));
  and and_1 (and_1_out, clock_1_out, ~rom_1_data[9]);  // AND_Gate
  Register A (.D(multiplexer_1_out), .en(demultiplexer_2_out0), .Q(A_q), .clk(clock_1_out));  // open: clr
  Register D (.D(demultiplexer_1_out1), .en(demultiplexer_2_out1), .Q(D_q), .clk(clock_1_out));  // open: clr
  PC pc_1 (.load(rom_1_data[9]), .\input (A_q), .clock(and_1_out), .reset(1'b0), .out(pc_1_out));
  Multiplexer #(.select(2), .width(8), .enable("false")) multiplexer_2 (
    .in0(A_q), .in1(D_q), .in2(ram_1_data), .out(multiplexer_2_out), .sel(rom_1_data[16:15]));  // open: in3
  Multiplexer #(.select(2), .width(8), .enable("false")) multiplexer_3 (
    .in0(A_q), .in1(D_q), .in2(ram_1_data), .out(multiplexer_3_out), .sel(rom_1_data[14:13]));  // open: in3
  Demultiplexer #(.select(2), .width(8), .enable("false")) demultiplexer_1 (
    .out0(demultiplexer_1_out0), .out1(demultiplexer_1_out1), .out2(demultiplexer_1_out2), .in(alu_1_output),
    .sel(rom_1_data[12:11]));  // open: out3
  alu alu_1 (
    .input1(multiplexer_2_out), .input2(multiplexer_3_out), .control(rom_1_data[29:26]),
    .\output (alu_1_output));  // open: compare_bits
  ROM #(.dataWidth(30)) rom_1 (.addr(pc_1_out), .data(rom_1_data), .sel(1'b1));
  Demultiplexer #(.select(2), .enable("false")) demultiplexer_2 (
    .out0(demultiplexer_2_out0), .out1(demultiplexer_2_out1), .out2(demultiplexer_2_out2), .in(1'b1),
    .sel(rom_1_data[12:11]));  // open: out3
  RAM #(.bus("separate")) ram_1 (
    .addr(A_q), .din(demultiplexer_1_out2), .data(ram_1_data), .str(demultiplexer_2_out2), .sel(1'b1),
    .clk(clock_1_out), .ld(demultiplexer_2_out2));  // open: clr

  // Notes on the sheet:
  //   contents of rom_1 (hex, n*v repeats v):
  //   60000 800 20000 1000 20000 800d000 120000 200
endmodule

module alu (
  input  [7:0] input1,
  input  [7:0] input2,
  input  [3:0] control,
  output [7:0] \output ,
  output [2:0] compare_bits
);

  wire [7:0] adder_1_out, and_1_out, multiplier_1_out, not_1_out, or_1_out, subtractor_1_out;

  Adder adder_1 (.a(input1), .b(input2), .out(adder_1_out));  // open: cin, cout
  Subtractor subtractor_1 (.a(input1), .b(input2), .out(subtractor_1_out));  // open: bin, bout
  Multiplier multiplier_1 (.a(input1), .b(input2), .out(multiplier_1_out));  // open: cin, cout
  assign and_1_out = input1 & input2;  // AND_Gate and_1, 8 bits wide
  assign or_1_out = input1 | input2;  // OR_Gate or_1, 8 bits wide
  assign not_1_out = ~input1;  // NOT_Gate not_1, 8 bits wide
  Comparator comparator_1 (.a(input1), .b(input2), .gt(compare_bits[0]), .eq(compare_bits[1]), .lt(compare_bits[2]));
  Multiplexer #(.select(4), .width(8), .enable("false")) multiplexer_1 (
    .in0(input1), .in1(input2), .in2(adder_1_out), .in3(subtractor_1_out), .in4(multiplier_1_out),
    .in5(and_1_out), .in6(or_1_out), .in7(not_1_out), .out(\output ), .sel(control));  // open: in8, in9, in10, in11, in12, in13, in14, in15
endmodule

module PC (
  input  load,
  input  [7:0] \input ,
  input  clock,
  input  reset,
  output [7:0] out
);

  wire not_1_out;

  not not_1 (not_1_out, load);
  Counter counter_1 (.load(load), .D(\input ), .count(not_1_out), .Q(out), .clk(clock), .clr(reset));  // open: carry
endmodule

module myCounter (
  input  increment,
  input  [7:0] in_2,
  input  load,
  input  reset,
  output [7:0] out
);

  wire [7:0] adder_1_out, multiplexer_1_out;

  Multiplexer #(.width(8), .enable("false")) multiplexer_1 (
    .in0(adder_1_out), .in1(in_2), .out(multiplexer_1_out), .sel(load));
  Register register_1 (.D(multiplexer_1_out), .en(1'b0), .Q(out), .clr(reset));  // open: clk
  Adder adder_1 (.a(out), .b(8'h1), .out(adder_1_out));  // open: cin, cout
endmodule
